# Fritzing sketch TTS_BreadBoard (saved by Fritzing 0.9.3b)
breadboards: 1

parts:
  U1 = NodeMCU V3.0
  DHT1 = DHT11 Humitidy and Temperature Sensor
  R1 = Photocell (LDR) [package=THT]
  LED1 = smd LED [color="Red (633nm)" package="1206 [SMD]"]  # not connected
  LED2 = smd LED [color="Red (633nm)" package="1206 [SMD]"]
  R2 = Resistor [tolerance=±5% resistance=220 package="2512 [SMD]"]
  R3 = Resistor [tolerance=±5% resistance=220 package="2512 [SMD]"]
  R4 = Resistor [tolerance=±5% resistance=220 package="2512 [SMD]"]

nets:
  N1: U1.D1, R2.Pin_0
  N2: U1.D2, R3.Pin_0
  N3: U1.D4, DHT1.DATA
  3V3: U1.3V3, DHT1.VDD
  GND: U1.GND, DHT1.GND
  N4: U1.RSV#40, R1.pin_0
  N5: U1.RSV#41, LED2.cathode, R4.Pin_1
  N6: U1.A0, R1.pin_1, R4.Pin_0
  N7: LED2.anode, R3.Pin_1

custom parts:
  NodeMCU V3.0: NodeMcu V3 Lua WIFI Development Board
  DHT11 Humitidy and Temperature Sensor: DHT11 Humidity and Temperature Sensor
